# Fritzing sketch circuit (saved by Fritzing 0.7.10b)
breadboards: 1

parts:
  Part1 = Electric Imp Breakout
  R1 = 4.7k Ω Resistor [package=THT]
  J1 = STARBOARD_GND [package=starboard_ground]  # not connected
  Q2 = NPN-Transistor [package="TO92 [THT]"]
  Q3 = NPN-Transistor [package="TO92 [THT]"]
  R2 = 4.7k Ω Resistor [package=THT]
  K1 = Relay [part_number=FRS1B-S package=THT]

nets:
  N1: Part1.6, Part1.9, R1.Pin_1, Q2.E, Q3.E, K1.C1, K1.C2
  N2: Part1.13, Part1.14
  N3: R1.Pin_0, Q3.B
  N4: Q2.B, Q3.C, R2.Pin_1
  N5: Q2.C, K1.COIL2
  N6: R2.Pin_0, K1.COIL1

notes:
  5Volts
  Garage Door

custom parts:
  Electric Imp Breakout: Electric Imp Breakout Board with onboard 3.3V regulated power supply
